// Logisim project Q2FSM.circ as structural Verilog: 1 circuit, main circuit main
module main (
  input  input_,
  input  reset,
  output [2:0] Q2next_Q1next_Q0next,
  output output_
);

  wire and_1_out, and_2_out, and_3_out, and_4_out, and_5_out, and_6_out, and_7_out, and_8_out, and_9_out,
       and_10_out, CLK_out, not_1_out, not_2_out, not_3_out, not_4_out, not_5_out, not_6_out, not_7_out,
       not_8_out, not_9_out, not_10_out, not_11_out, not_12_out, not_13_out, not_14_out, not_15_out,
       not_16_out, not_17_out, not_18_out, not_19_out, not_20_out, or_1_out, or_2_out, or_3_out, or_4_out,
       or_5_out, or_6_out, or_7_out;

  not not_1 (not_1_out, input_);
  not not_2 (not_2_out, Q2next_Q1next_Q0next[1]);
  not not_3 (not_3_out, Q2next_Q1next_Q0next[2]);
  not not_4 (not_4_out, Q2next_Q1next_Q0next[0]);
  not not_5 (not_5_out, Q2next_Q1next_Q0next[1]);
  not not_6 (not_6_out, Q2next_Q1next_Q0next[2]);
  not not_7 (not_7_out, Q2next_Q1next_Q0next[0]);
  not not_8 (not_8_out, Q2next_Q1next_Q0next[1]);
  not not_9 (not_9_out, Q2next_Q1next_Q0next[2]);
  not not_10 (not_10_out, Q2next_Q1next_Q0next[2]);
  not not_11 (not_11_out, Q2next_Q1next_Q0next[1]);
  not not_12 (not_12_out, Q2next_Q1next_Q0next[2]);
  not not_13 (not_13_out, Q2next_Q1next_Q0next[0]);
  not not_14 (not_14_out, Q2next_Q1next_Q0next[1]);
  not not_15 (not_15_out, Q2next_Q1next_Q0next[1]);
  not not_16 (not_16_out, Q2next_Q1next_Q0next[2]);
  not not_17 (not_17_out, Q2next_Q1next_Q0next[0]);
  not not_18 (not_18_out, Q2next_Q1next_Q0next[1]);
  not not_19 (not_19_out, Q2next_Q1next_Q0next[0]);
  not not_20 (not_20_out, Q2next_Q1next_Q0next[2]);
  and and_1 (and_1_out, input_, Q2next_Q1next_Q0next[0], not_2_out, not_3_out);
  and and_2 (and_2_out, input_, not_4_out, not_5_out, not_6_out);
  and and_3 (and_3_out, not_1_out, not_7_out, not_8_out, Q2next_Q1next_Q0next[2]);
  and and_4 (and_4_out, not_1_out, Q2next_Q1next_Q0next[0], Q2next_Q1next_Q0next[1], not_9_out);
  and and_5 (and_5_out, input_, Q2next_Q1next_Q0next[0], Q2next_Q1next_Q0next[1], not_10_out);
  and and_6 (and_6_out, input_, Q2next_Q1next_Q0next[0], not_11_out, not_12_out);
  and and_7 (and_7_out, not_1_out, not_13_out, not_14_out, Q2next_Q1next_Q0next[2]);
  and and_8 (and_8_out, not_1_out, Q2next_Q1next_Q0next[0], not_15_out, not_16_out);
  or or_1 (or_1_out, and_1_out, and_2_out);
  or or_2 (or_2_out, and_3_out, and_4_out);
  or or_3 (or_3_out, and_5_out, and_6_out);
  or or_4 (or_4_out, and_7_out, and_8_out);
  and and_9 (and_9_out, input_, not_17_out, not_18_out, Q2next_Q1next_Q0next[2]);
  and and_10 (and_10_out, not_1_out, not_19_out, Q2next_Q1next_Q0next[1], not_20_out);
  or or_5 (or_5_out, and_9_out, and_10_out);
  Clock CLK (.out(CLK_out));
  or or_6 (or_6_out, or_1_out, or_2_out);
  or or_7 (or_7_out, or_3_out, or_4_out);
  D_Flip_Flop Q0_next (.D(or_6_out), .clk(CLK_out), .Q(Q2next_Q1next_Q0next[0]), .reset(reset));  // open: Qn, preset
  D_Flip_Flop Q1_next (.D(or_7_out), .clk(CLK_out), .Q(Q2next_Q1next_Q0next[1]), .reset(reset));  // open: Qn, preset
  D_Flip_Flop Q2_next (.D(or_5_out), .clk(CLK_out), .Q(Q2next_Q1next_Q0next[2]), .reset(reset));  // open: Qn, preset
  nor nor_1 (output_, Q2next_Q1next_Q0next[0], Q2next_Q1next_Q0next[1], Q2next_Q1next_Q0next[2]);

  // Notes on the sheet:
  //   Marco Caniglia
  //   260 929 489
  //   F0
  //   F1
  //   F2
endmodule
